# Fritzing sketch sketch (saved by Fritzing 0.8.3b)
breadboards: 1

parts:
  U5 = mystery part, 3 pins [chip_label=DS18B20 spacing=300mil]
  R5 = Resistor [tolerance=±5% resistance=4.7k package=THT]
  Часть1 = DeuLigne 1.1 - The Snootlab's LCD shield for Arduino
  U7 = RELAY-SOLIDSTATE [part_number="SSR 25A 250V" package=relay-s108t02]
  Часть2 = Bluetooth Mate Silver
  L1 = Inductor [part_number="Heating element" package="400 mil [THT]"]
  Power_plug1 = Power plug [part_number=220V]

nets:
  +5V: U5.pin1, R5.Pin_0, Часть1.+5V, U7.-, Часть2.VCC
  N1: U5.pin2, R5.Pin_1, Часть1.D11_MOSI
  GND: U5.pin3, Часть1.GND, Часть2.GND
  N2: Часть1.D0_RX, Часть2.TX_5V
  N3: Часть1.D1_TX, Часть2.RX_5V
  N4: U7.T1, Power_plug1.VCC
  N5: U7.T2, L1.pin_1
  N6: L1.pin_0, Power_plug1.GND
